# Fritzing sketch ADXL345 (saved by Fritzing 0.9.0b)

parts:
  U1 = ADXL345 [package=lga14]
  Raspberry_Pi1 = Raspberry Pi B rev2

nets:
  VDD: U1.VDD, Raspberry_Pi1.5V
  GND: U1.GND, U1.SDO, Raspberry_Pi1.GND
  VSS: U1.VSS, U1.CS, Raspberry_Pi1.3V3
  N1: U1.SDA, Raspberry_Pi1.GPIO_2
  N2: U1.SCL, Raspberry_Pi1.GPIO_3
