# Fritzing sketch PattyL293D_Test (saved by Fritzing 0.9.0b)
circuit board: 8.46667cm x 5.64444cm
breadboards: 1

parts:
  Part1 = Breadboard Power Supply Board SMD
  IC1 = L293D [package=THT]
  D1 = Rectifier Diode [part_number=1N4001 package="Melf DO-213 AB [SMD]"]
  D2 = Rectifier Diode [part_number=1N4001 package="Melf DO-213 AB [SMD]"]
  D3 = Rectifier Diode [part_number=1N4001 package="Melf DO-213 AB [SMD]"]
  D4 = Rectifier Diode [part_number=1N4001 package="Melf DO-213 AB [SMD]"]
  M1 = DC Motor
  Raspberry_Pi1 = Raspberry Pi B rev2

nets:
  GND: Part1.GND, IC1.0V, D2.anode, D4.anode, Raspberry_Pi1.GND
  N1: Part1.VCC, IC1.+Vmotor, IC1.+V, D1.cathode, D3.cathode
  N2: IC1.Enable_1, Raspberry_Pi1.GPIO_27
  N3: IC1.In_1, Raspberry_Pi1.GPIO_17
  N4: IC1.Out_1_(_Controlled_by_Enable_1_), D3.anode, D4.cathode, M1.pin_2
  N5: IC1.Out_2_(_Controlled_by_Enable_1_), D1.anode, D2.cathode, M1.pin_1
  N6: IC1.In_2, Raspberry_Pi1.GPIO_18
