# Fritzing sketch Test-74HC595 (saved by Fritzing 0.9.0b)
breadboards: 1

parts:
  U1 = 7-SEGMENT-DISPLAY [package=7-segment-display]
  U2 = 74HC595 [package="DIP16 [THT]"]
  R1 = Resistor [tolerance=±5% resistance=220 package=THT]
  R2 = Resistor [tolerance=±5% resistance=220 package=THT]
  R3 = Resistor [tolerance=±5% resistance=220 package=THT]
  Raspberry_Pi1 = Raspberry Pi B rev2
  R8 = Resistor [tolerance=±5% resistance=220 package=THT]
  R9 = Resistor [tolerance=±5% resistance=220 package=THT]
  R10 = Resistor [tolerance=±5% resistance=220 package=THT]
  R11 = Resistor [tolerance=±5% resistance=220 package=THT]
  R12 = Resistor [tolerance=±5% resistance=220 package=THT]

nets:
  N1: U1.E, R1.Pin_1
  N2: U1.D, R3.Pin_1
  N3: U1.G1, R8.Pin_1
  GND: U1.C, U2.GND, Raspberry_Pi1.GND
  N4: U1.DP, R12.Pin_1
  N5: U1.B, R11.Pin_1
  N6: U1.A, R9.Pin_1
  N7: U1.G2, R10.Pin_1
  N8: U1.G, R2.Pin_1
  N9: U2.Q1, R8.Pin_0
  N10: U2.Q2, R12.Pin_0
  N11: U2.Q3, R9.Pin_0
  N12: U2.Q4, R10.Pin_0
  N13: U2.Q5, R2.Pin_0
  N14: U2.Q6, R1.Pin_0
  N15: U2.Q7, R11.Pin_0
  N16: U2.MR, Raspberry_Pi1.GPIO_25
  N17: U2.SH_CP, Raspberry_Pi1.GPIO_24
  N18: U2.ST_CP, Raspberry_Pi1.GPIO_23
  N19: U2.OE, Raspberry_Pi1.GPIO_8
  N20: U2.DS, Raspberry_Pi1.GPIO_18
  N21: U2.Q0, R3.Pin_0
  VCC: U2.VCC, Raspberry_Pi1.5V
